// Digital circuit 16-bit_barrel-left.dig as structural Verilog
module _16_bit_barrel_left (
  input  [15:0] A,
  input  [3:0] B,
  output [15:0] RESULT
);

  wire multiplexer_1_out, multiplexer_3_out, multiplexer_4_out, multiplexer_5_out, multiplexer_7_out,
       multiplexer_8_out, multiplexer_9_out, multiplexer_11_out, multiplexer_12_out, multiplexer_13_out,
       multiplexer_15_out, multiplexer_16_out, multiplexer_17_out, multiplexer_19_out, multiplexer_20_out,
       multiplexer_21_out, multiplexer_23_out, multiplexer_24_out, multiplexer_25_out, multiplexer_27_out,
       multiplexer_28_out, multiplexer_29_out, multiplexer_31_out, multiplexer_32_out, multiplexer_33_out,
       multiplexer_35_out, multiplexer_36_out, multiplexer_37_out, multiplexer_39_out, multiplexer_40_out,
       multiplexer_41_out, multiplexer_43_out, multiplexer_44_out, multiplexer_45_out, multiplexer_47_out,
       multiplexer_48_out, multiplexer_49_out, multiplexer_51_out, multiplexer_52_out, multiplexer_53_out,
       multiplexer_55_out, multiplexer_56_out, multiplexer_57_out, multiplexer_59_out, multiplexer_60_out,
       multiplexer_61_out, multiplexer_63_out, multiplexer_64_out;

  Multiplexer multiplexer_1 (.sel(B[1]), .in_0(multiplexer_4_out), .in_1(multiplexer_12_out), .out(multiplexer_1_out));
  Multiplexer multiplexer_2 (.sel(B[0]), .in_0(multiplexer_1_out), .in_1(multiplexer_5_out), .out(RESULT[15]));
  Multiplexer multiplexer_3 (.sel(B[3]), .in_0(A[15]), .in_1(A[7]), .out(multiplexer_3_out));
  Multiplexer multiplexer_4 (.sel(B[2]), .in_0(multiplexer_3_out), .in_1(multiplexer_19_out), .out(multiplexer_4_out));
  Multiplexer multiplexer_5 (.sel(B[1]), .in_0(multiplexer_8_out), .in_1(multiplexer_16_out), .out(multiplexer_5_out));
  Multiplexer multiplexer_6 (.sel(B[0]), .in_0(multiplexer_5_out), .in_1(multiplexer_9_out), .out(RESULT[14]));
  Multiplexer multiplexer_7 (.sel(B[3]), .in_0(A[14]), .in_1(A[6]), .out(multiplexer_7_out));
  Multiplexer multiplexer_8 (.sel(B[2]), .in_0(multiplexer_7_out), .in_1(multiplexer_23_out), .out(multiplexer_8_out));
  Multiplexer multiplexer_9 (.sel(B[1]), .in_0(multiplexer_12_out), .in_1(multiplexer_20_out), .out(multiplexer_9_out));
  Multiplexer multiplexer_10 (.sel(B[0]), .in_0(multiplexer_9_out), .in_1(multiplexer_13_out), .out(RESULT[13]));
  Multiplexer multiplexer_11 (.sel(B[3]), .in_0(A[13]), .in_1(A[5]), .out(multiplexer_11_out));
  Multiplexer multiplexer_12 (
    .sel(B[2]), .in_0(multiplexer_11_out), .in_1(multiplexer_27_out), .out(multiplexer_12_out));
  Multiplexer multiplexer_13 (
    .sel(B[1]), .in_0(multiplexer_16_out), .in_1(multiplexer_24_out), .out(multiplexer_13_out));
  Multiplexer multiplexer_14 (.sel(B[0]), .in_0(multiplexer_13_out), .in_1(multiplexer_17_out), .out(RESULT[12]));
  Multiplexer multiplexer_15 (.sel(B[3]), .in_0(A[12]), .in_1(A[4]), .out(multiplexer_15_out));
  Multiplexer multiplexer_16 (
    .sel(B[2]), .in_0(multiplexer_15_out), .in_1(multiplexer_31_out), .out(multiplexer_16_out));
  Multiplexer multiplexer_17 (
    .sel(B[1]), .in_0(multiplexer_20_out), .in_1(multiplexer_28_out), .out(multiplexer_17_out));
  Multiplexer multiplexer_18 (.sel(B[0]), .in_0(multiplexer_17_out), .in_1(multiplexer_21_out), .out(RESULT[11]));
  Multiplexer multiplexer_19 (.sel(B[3]), .in_0(A[11]), .in_1(A[3]), .out(multiplexer_19_out));
  Multiplexer multiplexer_20 (
    .sel(B[2]), .in_0(multiplexer_19_out), .in_1(multiplexer_35_out), .out(multiplexer_20_out));
  Multiplexer multiplexer_21 (
    .sel(B[1]), .in_0(multiplexer_24_out), .in_1(multiplexer_32_out), .out(multiplexer_21_out));
  Multiplexer multiplexer_22 (.sel(B[0]), .in_0(multiplexer_21_out), .in_1(multiplexer_25_out), .out(RESULT[10]));
  Multiplexer multiplexer_23 (.sel(B[3]), .in_0(A[10]), .in_1(A[2]), .out(multiplexer_23_out));
  Multiplexer multiplexer_24 (
    .sel(B[2]), .in_0(multiplexer_23_out), .in_1(multiplexer_39_out), .out(multiplexer_24_out));
  Multiplexer multiplexer_25 (
    .sel(B[1]), .in_0(multiplexer_28_out), .in_1(multiplexer_36_out), .out(multiplexer_25_out));
  Multiplexer multiplexer_26 (.sel(B[0]), .in_0(multiplexer_25_out), .in_1(multiplexer_29_out), .out(RESULT[9]));
  Multiplexer multiplexer_27 (.sel(B[3]), .in_0(A[9]), .in_1(A[1]), .out(multiplexer_27_out));
  Multiplexer multiplexer_28 (
    .sel(B[2]), .in_0(multiplexer_27_out), .in_1(multiplexer_43_out), .out(multiplexer_28_out));
  Multiplexer multiplexer_29 (
    .sel(B[1]), .in_0(multiplexer_32_out), .in_1(multiplexer_40_out), .out(multiplexer_29_out));
  Multiplexer multiplexer_30 (.sel(B[0]), .in_0(multiplexer_29_out), .in_1(multiplexer_33_out), .out(RESULT[8]));
  Multiplexer multiplexer_31 (.sel(B[3]), .in_0(A[8]), .in_1(A[0]), .out(multiplexer_31_out));
  Multiplexer multiplexer_32 (
    .sel(B[2]), .in_0(multiplexer_31_out), .in_1(multiplexer_47_out), .out(multiplexer_32_out));
  Multiplexer multiplexer_33 (
    .sel(B[1]), .in_0(multiplexer_36_out), .in_1(multiplexer_44_out), .out(multiplexer_33_out));
  Multiplexer multiplexer_34 (.sel(B[0]), .in_0(multiplexer_33_out), .in_1(multiplexer_37_out), .out(RESULT[7]));
  Multiplexer multiplexer_35 (.sel(B[3]), .in_0(A[7]), .in_1(1'b0), .out(multiplexer_35_out));
  Multiplexer multiplexer_36 (
    .sel(B[2]), .in_0(multiplexer_35_out), .in_1(multiplexer_51_out), .out(multiplexer_36_out));
  Multiplexer multiplexer_37 (
    .sel(B[1]), .in_0(multiplexer_40_out), .in_1(multiplexer_48_out), .out(multiplexer_37_out));
  Multiplexer multiplexer_38 (.sel(B[0]), .in_0(multiplexer_37_out), .in_1(multiplexer_41_out), .out(RESULT[6]));
  Multiplexer multiplexer_39 (.sel(B[3]), .in_0(A[6]), .in_1(1'b0), .out(multiplexer_39_out));
  Multiplexer multiplexer_40 (
    .sel(B[2]), .in_0(multiplexer_39_out), .in_1(multiplexer_55_out), .out(multiplexer_40_out));
  Multiplexer multiplexer_41 (
    .sel(B[1]), .in_0(multiplexer_44_out), .in_1(multiplexer_52_out), .out(multiplexer_41_out));
  Multiplexer multiplexer_42 (.sel(B[0]), .in_0(multiplexer_41_out), .in_1(multiplexer_45_out), .out(RESULT[5]));
  Multiplexer multiplexer_43 (.sel(B[3]), .in_0(A[5]), .in_1(1'b0), .out(multiplexer_43_out));
  Multiplexer multiplexer_44 (
    .sel(B[2]), .in_0(multiplexer_43_out), .in_1(multiplexer_59_out), .out(multiplexer_44_out));
  Multiplexer multiplexer_45 (
    .sel(B[1]), .in_0(multiplexer_48_out), .in_1(multiplexer_56_out), .out(multiplexer_45_out));
  Multiplexer multiplexer_46 (.sel(B[0]), .in_0(multiplexer_45_out), .in_1(multiplexer_49_out), .out(RESULT[4]));
  Multiplexer multiplexer_47 (.sel(B[3]), .in_0(A[4]), .in_1(1'b0), .out(multiplexer_47_out));
  Multiplexer multiplexer_48 (
    .sel(B[2]), .in_0(multiplexer_47_out), .in_1(multiplexer_63_out), .out(multiplexer_48_out));
  Multiplexer multiplexer_49 (
    .sel(B[1]), .in_0(multiplexer_52_out), .in_1(multiplexer_60_out), .out(multiplexer_49_out));
  Multiplexer multiplexer_50 (.sel(B[0]), .in_0(multiplexer_49_out), .in_1(multiplexer_53_out), .out(RESULT[3]));
  Multiplexer multiplexer_51 (.sel(B[3]), .in_0(A[3]), .in_1(1'b0), .out(multiplexer_51_out));
  Multiplexer multiplexer_52 (.sel(B[2]), .in_0(multiplexer_51_out), .in_1(1'b0), .out(multiplexer_52_out));
  Multiplexer multiplexer_53 (
    .sel(B[1]), .in_0(multiplexer_56_out), .in_1(multiplexer_64_out), .out(multiplexer_53_out));
  Multiplexer multiplexer_54 (.sel(B[0]), .in_0(multiplexer_53_out), .in_1(multiplexer_57_out), .out(RESULT[2]));
  Multiplexer multiplexer_55 (.sel(B[3]), .in_0(A[2]), .in_1(1'b0), .out(multiplexer_55_out));
  Multiplexer multiplexer_56 (.sel(B[2]), .in_0(multiplexer_55_out), .in_1(1'b0), .out(multiplexer_56_out));
  Multiplexer multiplexer_57 (.sel(B[1]), .in_0(multiplexer_60_out), .in_1(1'b0), .out(multiplexer_57_out));
  Multiplexer multiplexer_58 (.sel(B[0]), .in_0(multiplexer_57_out), .in_1(multiplexer_61_out), .out(RESULT[1]));
  Multiplexer multiplexer_59 (.sel(B[3]), .in_0(A[1]), .in_1(1'b0), .out(multiplexer_59_out));
  Multiplexer multiplexer_60 (.sel(B[2]), .in_0(multiplexer_59_out), .in_1(1'b0), .out(multiplexer_60_out));
  Multiplexer multiplexer_61 (.sel(B[1]), .in_0(multiplexer_64_out), .in_1(1'b0), .out(multiplexer_61_out));
  Multiplexer multiplexer_62 (.sel(B[0]), .in_0(multiplexer_61_out), .in_1(1'b0), .out(RESULT[0]));
  // NotConnected on nothing
  Multiplexer multiplexer_63 (.sel(B[3]), .in_0(A[0]), .in_1(1'b0), .out(multiplexer_63_out));
  Multiplexer multiplexer_64 (.sel(B[2]), .in_0(multiplexer_63_out), .in_1(1'b0), .out(multiplexer_64_out));

  // Notes on the sheet:
  //   A: First input to ALU
  //   B: Second input to ALU
  //   RESULT: The result of this ALU operation
  //   Shift left 8 bits
  //   Shift left 4 bits
  //   Shift left 2 bits
  //   Shift left 1 bit
endmodule

/* Test case 16 shift:
A B RESULT
loop(a,256)
loop(b,16)
(a) (b) (a << b)
end loop
end loop
*/
