// Digital circuit Increment-extended.dig as structural Verilog
module Increment_extended (
  input  [15:0] IMM,
  input  [15:0] A,
  input  [15:0] B,
  input  ALUIMM,
  input  MEMIMM,
  input  IMMFLIP,
  output [15:0] A_out,
  output [15:0] B_out
);

  wire LDR, not_1_out, STR;
  wire [15:0] multiplexer_1_out, multiplexer_2_out, multiplexer_3_out, multiplexer_4_out, multiplexer_5_out,
       multiplexer_6_out, multiplexer_7_out;

  Multiplexer #(.Bits(16)) multiplexer_1 (.sel(ALUIMM), .in_0(A), .in_1(IMM), .out(multiplexer_1_out));
  Multiplexer #(.Bits(16)) multiplexer_2 (.sel(STR), .in_0(B), .in_1(IMM), .out(multiplexer_2_out));
  Multiplexer #(.Bits(16)) multiplexer_3 (.sel(STR), .in_0(A), .in_1(B), .out(multiplexer_3_out));
  Multiplexer #(.Bits(16)) multiplexer_4 (.sel(LDR), .in_0(A), .in_1(IMM), .out(multiplexer_4_out));
  and and_1 (LDR, IMMFLIP, MEMIMM);
  and and_2 (STR, not_1_out, MEMIMM);
  not not_1 (not_1_out, IMMFLIP);
  Multiplexer #(.Bits(16)) multiplexer_5 (.sel(ALUIMM), .in_0(B), .in_1(multiplexer_1_out), .out(multiplexer_5_out));
  Multiplexer #(.Bits(16)) multiplexer_6 (.sel(ALUIMM), .in_0(A), .in_1(B), .out(multiplexer_6_out));
  Multiplexer #(.Bits(16)) multiplexer_7 (
    .sel(LDR), .in_0(multiplexer_3_out), .in_1(multiplexer_4_out), .out(multiplexer_7_out));
  Multiplexer #(.Bits(16)) multiplexer_8 (
    .sel(ALUIMM), .in_0(multiplexer_2_out), .in_1(multiplexer_5_out), .out(B_out));
  Multiplexer #(.Bits(16)) multiplexer_9 (
    .sel(ALUIMM), .in_0(multiplexer_7_out), .in_1(multiplexer_6_out), .out(A_out));

  // Other names for the same wires on the sheet: AL = ALUIMM; ME = MEMIMM

  // Notes on the sheet:
  //   IMM: The Imm value
  //   A_out: choosing between the ALU result (for immediates) or the IN
  //   A: the register value read by RS1
  //   B: the register value read by RS2
  //   B_out: choosing between the ALU result (for immediates) or the IN
  //   ALUIMM: HIGH if is an ALU Immediate instruction
  //   MEMIMM: HIGH if is an MEM Immediate instruction
  //   Choose between the default A / IMM for LDR
  //   Isolate the I-MEM instructions
  //   Choose between the normal input / Imm
  //   B needs to flip to A becuase of how the ALU is made
  //   More flips for the STR instruction to get the correct ADDRESS  & VALUE
  //   Choosen between STR or LDR
  //   Choose between ALU IMM or I-MEM IMM output
endmodule
