// Digital circuit PC.dig as structural Verilog
module PC (
  input  [15:0] IN,
  input  WE,
  input  clk,
  output [15:0] ADR
);

  wire not_1_out;
  wire [15:0] multiplexer_1_out, plus_1_s;

  not not_1 (not_1_out, WE);
  Multiplexer #(.Bits(16)) multiplexer_1 (.sel(not_1_out), .in_0(IN), .in_1(plus_1_s), .out(multiplexer_1_out));
  Register #(.Bits(16), .isProgramCounter("true")) PC (.D(multiplexer_1_out), .C(clk), .en(1'b1), .Q(ADR));
  Add #(.Bits(16)) plus_1 (.a(16'h1), .b(ADR), .c_i(1'b0), .s(plus_1_s));  // open: c_o
  // NotConnected on nothing

  // Notes on the sheet:
  //   IN: The value to be saved into the register specified by WS if WE is high,
  //   WE: Write ENABLE (passed from reg file)
  //   ADR: Address the PC points to
endmodule
