// Digital circuit alu-extended.dig as structural Verilog
module alu_extended (
  input  [15:0] A,
  input  [15:0] B,
  input  [2:0] ALUOP,
  output [15:0] RESULT,
  output [3:0] FLAG
);

  wire add_1_c_o, and_2_out, or_2_out, or_3_out, xnor_2_out, xor_2_out;
  wire [15:0] add_1_s, and_1_out, multiplexer_1_out, nand_1_out, nor_1_out, not_1_out, or_1_out, xnor_1_out,
       xor_1_out;

  assign not_1_out = ~B;  // Not not_1, 16 bits wide
  Multiplexer #(.Bits(16)) multiplexer_1 (.sel(ALUOP[0]), .in_0(B), .in_1(not_1_out), .out(multiplexer_1_out));
  assign and_1_out = A & B;  // And and_1, 16 bits wide
  assign or_1_out = A | B;  // Or or_1, 16 bits wide
  assign xor_1_out = A ^ B;  // XOr xor_1, 16 bits wide
  assign nand_1_out = ~(A & B);  // NAnd nand_1, 16 bits wide
  assign nor_1_out = ~(A | B);  // NOr nor_1, 16 bits wide
  assign xnor_1_out = ~(A ^ B);  // XNOr xnor_1, 16 bits wide
  Add #(.Bits(16)) add_1 (.a(A), .b(multiplexer_1_out), .c_i(ALUOP[0]), .s(add_1_s), .c_o(add_1_c_o));
  xnor xnor_2 (xnor_2_out, multiplexer_1_out[15], A[15]);
  xor xor_2 (xor_2_out, A[15], add_1_s[15]);
  Multiplexer #(.Selector_Bits(3), .Bits(16)) multiplexer_2 (
    .sel(ALUOP), .in_0(add_1_s), .in_1(add_1_s), .in_2(and_1_out), .in_3(or_1_out), .in_4(xor_1_out),
    .in_5(nand_1_out), .in_6(nor_1_out), .in_7(xnor_1_out), .out({FLAG[1], RESULT[14:0]}));
  and and_2 (and_2_out, xnor_2_out, xor_2_out);
  or or_2 (or_2_out, ALUOP[1], ALUOP[2]);
  Multiplexer multiplexer_3 (.sel(or_2_out), .in_0(and_2_out), .in_1(1'b0), .out(FLAG[3]));
  Multiplexer multiplexer_4 (.sel(or_2_out), .in_0(add_1_c_o), .in_1(1'b0), .out(FLAG[2]));
  or or_3 (or_3_out, RESULT[0], RESULT[1], RESULT[2], RESULT[3], RESULT[4], RESULT[5], RESULT[6], RESULT[7], RESULT[8], RESULT[9], RESULT[10], RESULT[11], RESULT[12], RESULT[13], RESULT[14], FLAG[1]);
  not not_2 (FLAG[0], or_3_out);
  // NotConnected on nothing
  // NotConnected on nothing

  assign RESULT[15] = FLAG[1];

  // Other names for the same wires on the sheet: S[2:0] = ALUOP; S0 = ALUOP[0]; S1 = ALUOP[1]; S2 = ALUOP[2]

  // Notes on the sheet:
  //   A: First input to ALU
  //   B: Second input to ALU
  //   ALUOP: Operation selection input
  //   RESULT: The result of this ALU operation
  //   FLAG: The flags associated with the result of this ALU operation
  //   0. Z (zero)
  //   1. N (negative)
  //   2. C (carry)
  //   3. V (overflow)
  //   Arithmetic logic
  //   Non-Arithmetic logic
  //   Overflow flag logic
  //   Carry flag logic
  //   Zero & Negative flag logic
  //   Z
  //   N
  //   C
  //   V
endmodule

/* Test case RESULT:
ALUOP A B RESULT

# Test small results
loop(a, 1 << 4)
  loop(b, 1 << 4)
    (0b000) (a) (b) ((a + b) & 0xFFFF)
    (0b001) (a) (b) ((a - b) & 0xFFFF)
    (0b010) (a) (b) (a & b)
    (0b011) (a) (b) (a | b)
    (0b100) (a) (b) (a ^ b)
    (0b101) (a) (b) (~(a & b))
    (0b110) (a) (b) (~(a | b))
    (0b111) (a) (b) (~(a ^ b))
  end loop
end loop


# Test large results
loop(i, 1000)
    let a = random(1 << 16);
    let b = random(1 << 16);

    (0b000) (a) (b) ((a + b) & 0xFFFF)
    (0b001) (a) (b) ((a - b) & 0xFFFF)
    (0b010) (a) (b) (a & b)
    (0b011) (a) (b) (a | b)
    (0b100) (a) (b) (a ^ b)
    (0b101) (a) (b) (~(a & b))
    (0b110) (a) (b) (~(a | b))
    (0b111) (a) (b) (~(a ^ b))
end loop
*/

/* Test case Z:
ALUOP A B Z

declare Z = FLAG & 0b1;

# Test all zero cases
0b000 0 0 1
0b001 0 0 1
0b010 0 0 1
0b011 0 0 1
0b100 0 0 1
0b101 0 0 0
0b110 0 0 0
0b111 0 0 0

# Test 1 + (-1) = 0
0b000 1 0xFFFF 1

# Test with a single bit set in A
loop(s, 16)
    let a = 1 << s;

    0b000 (a) 0 (a = 0)
    0b001 (a) 0 (a = 0)
    0b010 (a) 0 1
    0b011 (a) 0 (a = 0)
    0b100 (a) 0 (a = 0)
    0b101 (a) 0 0
    0b110 (a) 0 0
    0b111 (a) 0 (a = 0)
end loop

# Test random inputs
loop(i, 200)
    let a = random(1 << 16);
    let b = random(1 << 16);

    0b000 (a) (b) (((a + b) & 0xFFFF) = 0)
    0b001 (a) (b) (((a - b) & 0xFFFF) = 0)
    0b010 (a) (b) ((a & b) = 0)
    0b011 (a) (b) ((a | b) = 0)
    0b100 (a) (b) ((a ^ b) = 0)
    0b101 (a) (b) (((~(a & b)) & 0xFFFF) = 0)
    0b110 (a) (b) (((~(a | b)) & 0xFFFF) = 0)
    0b111 (a) (b) (((~(a ^ b)) & 0xFFFF) = 0)
end loop
*/

/* Test case N:
ALUOP A B N

declare N = (FLAG >> 1) & 0b1;

# Test all zero cases
0b000 0 0 0
0b001 0 0 0
0b010 0 0 0
0b011 0 0 0
0b100 0 0 0
0b101 0 0 1
0b110 0 0 1
0b111 0 0 1

# Test 1 + (-1) = 0
0b000 1 0xFFFF 0

# Test with a single bit set in A
loop(s, 16)
    let a = 1 << s;

    0b000 (a) 0 ((a >> 15) & 0b1)
    0b001 (a) 0 ((a >> 15) & 0b1)
    0b010 (a) 0 0
    0b011 (a) 0 ((a >> 15) & 0b1)
    0b100 (a) 0 ((a >> 15) & 0b1)
    0b101 (a) 0 1
    0b110 (a) 0 ((~(a >> 15)) & 0b1)
    0b111 (a) 0 ((~(a >> 15)) & 0b1)
end loop

# Test random inputs
loop(i, 200)
    let a = random(1 << 16);
    let b = random(1 << 16);

    0b000 (a) (b) (((a + b) >> 15) & 0b1)
    0b001 (a) (b) (((a - b) >> 15) & 0b1)
    0b010 (a) (b) (((a & b) >> 15) & 0b1)
    0b011 (a) (b) (((a | b) >> 15) & 0b1)
    0b100 (a) (b) (((a ^ b) >> 15) & 0b1)
    0b101 (a) (b) (((~(a & b)) >> 15) & 0b1)
    0b110 (a) (b) (((~(a | b)) >> 15) & 0b1)
    0b111 (a) (b) (((~(a ^ b)) >> 15) & 0b1)
end loop
*/

/* Test case C:
ALUOP A B C

declare C = (FLAG >> 2) & 0b1;

# Test 0 + 0
0b000 0 0 0

# (0 - 0) is implemented as 0 + (0xFFFF + 1), so a carry is expected
0b001 0 0 1

# Carry should propagate all the way from the first bit if necessary
0b000 1 0xFFFF 1

# Test with a single bit set in A
loop(s, 16)
    let a = 1 << s;

    0b000 (a) 0 0
    0b001 (a) 0 1  # (a - 0) is implemented as (a + 0xFFFF + 1) in the adder, so a carry is always expected
    0b010 (a) 0 0  # carry is defined as 0 for AND
    0b011 (a) 0 0  # carry is defined as 0 for OR
    0b100 (a) 0 0  # carry is defined as 0 for XOR
    0b101 (a) 0 0  # carry is defined as 0 for NAND
    0b110 (a) 0 0  # carry is defined as 0 for NOR
    0b111 (a) 0 0  # carry is defined as 0 for XNOR
end loop

# Adding 15 bit values should never carry
loop(i, 100)
    0b000 (random(1 << 15)) (random(1 << 15)) 0
end loop

# Test random inputs
loop(i, 200)
    let a = random(1 << 16);
    let b = random(1 << 16);

    0b000 (a) (b) (((a + b) >> 16) & 0b1)
    0b001 (a) (b) (~((a - b) >> 16) & 0b1)
end loop

# AND, OR, XOR, and their N versions never set carry
loop(i, 100)
    let a = random(1 << 16);
    let b = random(1 << 16);
    0b010 (a) (b) 0
    0b011 (a) (b) 0
    0b100 (a) (b) 0
    0b101 (a) (b) 0
    0b110 (a) (b) 0
    0b111 (a) (b) 0
end loop
*/

/* Test case V:
ALUOP A B V

declare V = (FLAG >> 3) & 0b1;

# Test zero cases for + / -
0b000 0 0 0
0b001 0 0 0

# 1 + (-1) = 0  ; different input signs = no overflow here!
0b000 1 0xFFFF 0

# 3 - 5 = 3 + (-5) = -2  ; subtraction inverts the second operand sign
0b001 3 5 0

# Some edge cases when subtracting 0x8000
0b001 0x8000 0x8000 0
0b001 0xFFFF 0x8000 0
0b001 0x7FFF 0x8000 1

# Test with a single bit set in A
loop(s, 16)
    let a = 1 << s;

    0b000 (a) 0 0
    0b001 (a) 0 0
    0b010 (a) 0 0  # overflow is defined as 0 for AND
    0b011 (a) 0 0  # overflow is defined as 0 for OR
    0b100 (a) 0 0  # overflow is defined as 0 for XOR
    0b101 (a) 0 0  # overflow is defined as 0 for NAND
    0b110 (a) 0 0  # overflow is defined as 0 for NOR
    0b111 (a) 0 0  # overflow is defined as 0 for XNOR
end loop

# Test random inputs
loop(i, 200)
    let a = random(1 << 16);
    let b = random(1 << 16);

    0b000 (a) (b) (((~(a ^ b) & (a ^ (a + b))) >> 15) & 0b1)
    0b001 (a) (b) (((~(a ^ ~b) & (a ^ (a - b))) >> 15) & 0b1)
end loop

# AND, OR, XOR, and their N versions never set overflow
loop(i, 100)
    let a = random(1 << 16);
    let b = random(1 << 16);
    0b010 (a) (b) 0
    0b011 (a) (b) 0
    0b100 (a) (b) 0
    0b101 (a) (b) 0
    0b110 (a) (b) 0
    0b111 (a) (b) 0
end loop
*/
