// Digital circuit barrel-shift.dig as structural Verilog
module barrel_shift (
  input  [15:0] A,
  input  [15:0] B,
  input  D,
  output [15:0] RESULT
);

  wire [15:0] _16_bit_barrel_left_1_result, _16_bit_barrel_right_1_result;

  _16_bit_barrel_left _16_bit_barrel_left_1 (.A(A), .B(B[3:0]), .RESULT(_16_bit_barrel_left_1_result));
  _16_bit_barrel_right _16_bit_barrel_right_1 (.A(A), .B(B[3:0]), .RESULT(_16_bit_barrel_right_1_result));
  Multiplexer #(.Bits(16)) multiplexer_1 (
    .sel(D), .in_0(_16_bit_barrel_left_1_result), .in_1(_16_bit_barrel_right_1_result), .out(RESULT));
  // NotConnected on nothing

  // Notes on the sheet:
  //   A: Number to be shifted
  //   B: Number of bits to be shifted (max of 4)
  //   RESULT: The result of this ALU operation
  //   D: Direction of the shift (left or right)
  //   We can only shift a maximum of 16 bits!!!!
endmodule

/* Test case 16 shift:
A B D RESULT
loop(a,256)
loop(b,16)
(a) (b) (1) (a >> b)
end loop
end loop
loop(a,256)
loop(b,16)
(a) (b) (0) (a << b)
end loop
end loop
*/
