// Digital circuit control_unit-extended.dig as structural Verilog
module control_unit_extended (
  input  [15:0] INST,
  input  ZREG,
  output [2:0] ALUOP,
  output [2:0] RS1,
  output [2:0] RS2,
  output [2:0] WS,
  output STR,
  output WE,
  output [1:0] DMUX,
  output LDR,
  output FLEN,
  output SETH,
  output D,
  output ALUIMM,
  output MEMIMM,
  output IMMFLIP
);

  wire and_1_out, and_2_out, and_3_out, and_4_out, and_5_out, and_6_out, and_7_out, and_12_out, nand_1_out,
       not_1_out, not_2_out, not_3_out, not_4_out, not_5_out, not_6_out, not_7_out, not_8_out, not_9_out,
       not_10_out, not_11_out, not_12_out, not_13_out, not_14_out, not_15_out, not_16_out, not_17_out,
       not_19_out, not_20_out, not_21_out, not_22_out, or_1_out, or_2_out;
  wire [2:0] multiplexer_2_out;

  not not_1 (not_1_out, INST[15]);
  not not_2 (not_2_out, INST[15]);
  not not_3 (not_3_out, INST[14]);
  not not_4 (not_4_out, ZREG);
  and and_1 (and_1_out, INST[14], not_1_out);
  and and_2 (and_2_out, not_2_out, not_3_out, INST[13], INST[12]);
  not not_5 (not_5_out, INST[15]);
  not not_6 (not_6_out, INST[13]);
  not not_7 (not_7_out, INST[12]);
  not not_8 (not_8_out, INST[15]);
  nand nand_1 (nand_1_out, not_4_out, INST[11]);
  and and_3 (and_3_out, not_5_out, INST[14], not_6_out, not_7_out);
  and and_4 (and_4_out, not_8_out, INST[14], INST[13], INST[12]);
  or or_1 (or_1_out, and_1_out, and_2_out);
  not not_9 (not_9_out, INST[7]);
  Multiplexer #(.Bits(3)) multiplexer_1 (.sel(or_1_out), .in_0(INST[2:0]), .in_1(INST[10:8]), .out(RS2));
  and and_5 (and_5_out, and_4_out, not_9_out);
  not not_10 (not_10_out, INST[15]);
  not not_11 (not_11_out, INST[13]);
  not not_12 (not_12_out, INST[15]);
  not not_13 (not_13_out, INST[14]);
  not not_14 (not_14_out, INST[13]);
  not not_15 (not_15_out, INST[12]);
  not not_16 (not_16_out, INST[15]);
  not not_17 (not_17_out, INST[14]);
  not not_18 (not_17_out, INST[14]);
  not not_19 (not_19_out, INST[13]);
  not not_20 (not_20_out, INST[15]);
  not not_21 (not_21_out, INST[15]);
  not not_22 (not_22_out, INST[14]);
  or or_2 (or_2_out, and_3_out, and_5_out);
  and and_6 (and_6_out, not_10_out, INST[14], not_11_out, INST[12]);
  and and_7 (and_7_out, not_12_out, not_13_out, not_14_out, not_15_out);
  and and_8 (SETH, not_16_out, not_17_out, not_19_out, INST[12]);
  and and_9 (MEMIMM, not_20_out, INST[14], INST[13], INST[12]);
  and and_10 (ALUIMM, not_21_out, not_22_out, INST[13], INST[12]);
  Multiplexer #(.Bits(3)) multiplexer_2 (.sel(INST[7]), .in_0(3'b000), .in_1(3'b001), .out(multiplexer_2_out));
  Multiplexer #(.Bits(3)) multiplexer_3 (.sel(nand_1_out), .in_0(3'b000), .in_1(INST[10:8]), .out(WS));
  Multiplexer #(.Bits(3)) multiplexer_4 (.sel(ALUIMM), .in_0(INST[14:12]), .in_1(multiplexer_2_out), .out(ALUOP));
  and and_11 (STR, nand_1_out, or_2_out);
  not not_23 (WE, STR);
  or or_3 (FLEN, INST[15], ALUIMM);
  and and_12 (and_12_out, MEMIMM, INST[7]);
  or or_4 (DMUX[0], and_6_out, and_12_out);
  or or_5 (DMUX[1], SETH, and_7_out);
  LED led_1 (.in(nand_1_out));
  // NotConnected on nothing
  // NotConnected on nothing
  // NotConnected on nothing
  // NotConnected on nothing
  // NotConnected on nothing
  // NotConnected on nothing
  // NotConnected on nothing
  // NotConnected on nothing
  // NotConnected on nothing
  // NotConnected on nothing
  // NotConnected on nothing
  // NotConnected on nothing
  // NotConnected on nothing
  // NotConnected on nothing

  assign D = INST[3];
  assign IMMFLIP = INST[7];
  assign LDR = 1'b1;
  assign RS1 = INST[6:4];

  // Notes on the sheet:
  //   FLEN: Checks whether the flag register should be written to or not
  //   only on ALU OP codes (1 0 x x)
  //   ZREG: ALU Flag
  //   SETH: the SETH instruction
  //   D: The direction for the Logical shift
  //   ALUIMM: Checks for if a ALU IMM instruction was called
  //   MEMIMM: Check if STR/LDR immediate instruction was called
  //   IMMFLIP: The IMM FLIP
  //   Make RD == RB on ALU/MEM IMM && MEM operations
  //   check for 0011<<12 || 0111<<12 | 0<<7
  //   Z
  //   RD
  //   RA
  //   RB
  //   opcode
  //   D
  //   IMM flip
  //   Testing for LDR
  //   Testing for MOV
  //   Testing for SETH
  //   Testing for STR/LDR IMM
  //   Testing for ADD/SUB IMM
  //   ALU IMMOP convert to ALUOP
  //   Choose zero register to write if cond == false
  //   Check 1xxx and 0011
  //   check for DMUX (LDR & MOVL || SETH)
  //   Direction for Logical shift (0 left, 1 right)
  //   Isolate the ALU/MEM IMM instructions
endmodule

/* Test case All Tests:
	INST                                    WE  ALUOP  RS1   RS2  WS  STR  LDR DMUX

let aluop  = 0b1000;
let ldrop  = 0b0101;
let strop  = 0b0100;
let movlop = 0b0000;

loop(rd, 1<<3)
loop(ra, 1<<3)
loop(rb, 1<<3)

loop(i, 4)
	((aluop+i)<<12 | rd<<8 | ra<<4 | rb<<0) 1  (i+8)     (ra)  (rb) (rd)  0   X    0  #test add/sub/and/orr
end loop

	(ldrop    <<12 | rd<<8 | ra<<4 )        1  X       (ra)  x    (rd)  0   1    1  #test ldr
	(strop    <<12 | rd<<8 | ra<<4 )        0  X       (ra)  (rd)  X    1   X    X  #test str
	
	let imm = random(256);
	(movlop   <<12 | rd<<8 | imm )          1  X       X      X   (rd)  0   X    2  #test movl

end loop
end loop
end loop
*/

/* Test case WS:
	INST                                    WS 

let aluop  = 0b1000;
let ldrop  = 0b0101;
let strop  = 0b0100;
let movlop = 0b0000;

loop(rd, 1<<3)
loop(ra, 1<<3)
loop(rb, 1<<3)

loop(i, 4)
	((aluop+i)<<12 | rd<<8 | ra<<4 | rb<<0) (rd)  #test add/sub/and/orr
end loop

	(ldrop    <<12 | rd<<8 | ra<<4 )        (rd)   #test ldr
	(strop    <<12 | rd<<8 | ra<<4 )        X     #test str
	
	let imm = random(256);
	(movlop   <<12 | rd<<8 | imm )          (rd)  #test movl

end loop
end loop
end loop
*/

/* Test case RS1:
	INST                                    RS1  

let aluop  = 0b1000;
let ldrop  = 0b0101;
let strop  = 0b0100;
let movlop = 0b0000;

loop(rd, 1<<3)
loop(ra, 1<<3)
loop(rb, 1<<3)

loop(i, 4)
	((aluop+i)<<12 | rd<<8 | ra<<4 | rb<<0) (ra)  #test add/sub/and/orr
end loop

	(ldrop    <<12 | rd<<8 | ra<<4 )        (ra)  #test ldr
	(strop    <<12 | rd<<8 | ra<<4 )        (ra)  #test str

end loop
end loop
end loop
*/

/* Test case RS2:
	INST                                    RS2  

let aluop  = 0b1000;
let ldrop  = 0b0101;
let strop  = 0b0100;
let movlop = 0b0000;

loop(rd, 1<<3)
loop(ra, 1<<3)
loop(rb, 1<<3)

loop(i, 4)
	((aluop+i)<<12 | rd<<8 | ra<<4 | rb<<0) (rb) #test add/sub/and/orr
end loop
	(strop    <<12 | rd<<8 | ra<<4 )        (rd) #test str

end loop
end loop
end loop
*/

/* Test case STR:
	INST                                    STR 

let aluop  = 0b1000;
let ldrop  = 0b0101;
let strop  = 0b0100;
let movlop = 0b0000;

loop(rd, 1<<3)
loop(ra, 1<<3)
loop(rb, 1<<3)

loop(i, 4)
	((aluop+i)<<12 | rd<<8 | ra<<4 | rb<<0) 0  #test add/sub/and/orr
end loop

	(ldrop    <<12 | rd<<8 | ra<<4 )        0  #test ldr
	(strop    <<12 | rd<<8 | ra<<4 )        1  #test str
	
	let imm = random(256);
	(movlop   <<12 | rd<<8 | imm )          0  #test movl

end loop
end loop
end loop
*/

/* Test case WE:
	INST                                    WE  

let aluop  = 0b1000;
let ldrop  = 0b0101;
let strop  = 0b0100;
let movlop = 0b0000;

loop(rd, 1<<3)
loop(ra, 1<<3)
loop(rb, 1<<3)

loop(i, 4)
	((aluop+i)<<12 | rd<<8 | ra<<4 | rb<<0) 1  #test add/sub/and/orr
end loop

	(ldrop    <<12 | rd<<8 | ra<<4 )        1  #test ldr
	(strop    <<12 | rd<<8 | ra<<4 )        0  #test str
	
	let imm = random(256);
	(movlop   <<12 | rd<<8 | imm )          1  #test movl

end loop
end loop
end loop
*/

/* Test case LDR:
	INST                                    LDR 

let aluop  = 0b1000;
let ldrop  = 0b0101;
let strop  = 0b0100;
let movlop = 0b0000;

loop(rd, 1<<3)
loop(ra, 1<<3)
loop(rb, 1<<3)

loop(i, 4)
	((aluop+i)<<12 | rd<<8 | ra<<4 | rb<<0) X    #test add/sub/and/orr
end loop

	(ldrop    <<12 | rd<<8 | ra<<4 )        1    #test ldr
	(strop    <<12 | rd<<8 | ra<<4 )        X    #test str
	
	let imm = random(256);
	(movlop   <<12 | rd<<8 | imm )          X    #test movl

end loop
end loop
end loop
*/

/* Test case DMUX:
	INST                                    DMUX

let aluop  = 0b1000;
let ldrop  = 0b0101;
let strop  = 0b0100;
let movlop = 0b0000;
let aluImm = 0b0011;
let memImm = 0b0111;

loop(rd, 1<<3)
loop(ra, 1<<3)
loop(rb, 1<<3)

loop(i, 4)
	((aluop+i)<<12 | rd<<8 | ra<<4 | rb<<0) 0  #test add/sub/and/orr
end loop

	(ldrop    <<12 | rd<<8 | ra<<4 )        1  #test ldr
	
	let imm = random(256);
	let immS = random(128);
	(movlop   <<12 | rd<<8 | imm )          2  #test movl
 	
	(aluImm   <<12 | rd<<8 | 1 << 7 | immS) 0
	(memImm   <<12 | rd<<8 | 0 << 7 | immS) 0
	(memImm   <<12 | rd<<8 | 1 << 7 | immS) 1
end loop
end loop
end loop
*/

/* Test case ALUOP:
	INST                                    ALUOP 

let aluop  = 0b1000;
let ldrop  = 0b0101;
let strop  = 0b0100;
let movlop = 0b0000;

loop(rd, 1<<3)
loop(ra, 1<<3)
loop(rb, 1<<3)

loop(i, 4)
	((aluop+i)<<12 | rd<<8 | ra<<4 | rb<<0) (i+8)    #test add/sub/and/orr
end loop

end loop
end loop
end loop
*/

/* Test case FLEN:
INST FLEN
(0b0011 << 12) (1)
(0b1000 << 12) (1)
(0b1001 << 12) (1)
(0b1010 << 12) (1)
(0b1011 << 12) (1)
(0b1100 << 12) (1)
(0b1101 << 12) (1)
(0b1110 << 12) (1)
(0b1111 << 12) (1)
*/

/* Test case SETH:
INST SETH
(0b0001 << 12) (1)
(0b1000 << 12) (0)
(0b1001 << 12) (0)
(0b1010 << 12) (0)
(0b1011 << 12) (0)
(0b1111 << 12) (0)
*/
