// Digital circuit cpu.dig as structural Verilog
module cpu (
  input  CLK
);

  wire control_unit_1_p3, control_unit_1_p7, control_unit_1_p8, control_unit_1_p10, control_unit_1_p11,
       control_unit_1_p12, Z_REG;
  wire [1:0] control_unit_1_p9;
  wire [2:0] control_unit_1_p4, control_unit_1_p5, control_unit_1_p6;
  wire [3:0] FLAG;
  wire [15:0] _1D, ALU_RES, INSTR, multiplexer_1_out, notconnected_1_out, reg_file_1_address,
       reg_file_1_out1, reg_file_1_out2;

  // control_unit control_unit_1: pin names not known; wires that end beside it: INSTR, Z_REG, control_unit_1_p3, control_unit_1_p4, control_unit_1_p5, control_unit_1_p6, control_unit_1_p7, control_unit_1_p8, control_unit_1_p9, control_unit_1_p10, control_unit_1_p11, control_unit_1_p12
  Multiplexer #(.Selector_Bits(2), .Bits(16)) multiplexer_1 (
    .sel(control_unit_1_p9), .in_0(ALU_RES), .in_1(_1D), .in_2({{8{1'b0}}, INSTR[7:0]}),
    .in_3(notconnected_1_out), .out(multiplexer_1_out));
  // NotConnected on notconnected_1_out
  // Probe DATA on multiplexer_1_out
  reg_file reg_file_1 (
    .RS1(control_unit_1_p4), .RS2(control_unit_1_p5), .WS(control_unit_1_p6), .WE(control_unit_1_p8),
    .IN(multiplexer_1_out), .clk(CLK), .FL_EN(control_unit_1_p11), .FL_IN(FLAG), .SETH(control_unit_1_p12),
    .OUT1(reg_file_1_out1), .OUT2(reg_file_1_out2), .Z_REG(Z_REG), .ADDRESS(reg_file_1_address));
  // alu alu_1: pin names not known; wires that end beside it: reg_file_1_out1, reg_file_1_out2, control_unit_1_p3, ALU_RES, FLAG, control_unit_1_p8, control_unit_1_p9, control_unit_1_p10, control_unit_1_p11, control_unit_1_p12
  RAMDualAccess #(.AddrBits(16), .isProgramMemory("true"), .Bits(16)) RAM (
    .str(control_unit_1_p7), .C(CLK), .ld(control_unit_1_p10), .A1(reg_file_1_out1), .Din1(reg_file_1_out2),
    .A2(reg_file_1_address), .D1(_1D), .D2(INSTR));

  // Notes on the sheet:
  //   You need to consider where to physically locate the flag register.
  //   Option 1: Top-level schematic
  //   If so, how do we read from it when executing an instruction?
  //   Option 2: Inside the register file
  //   If so, how does the ALU write to it after each instruction?
  //   You might need to make some changes to the register file to allow the ALU to write, and the CPU to read from the flag register.
  //   Also, you likely need to add another 1-bit control signal (we suggest the name FLEN) that controls 
  //   if the flag register is updated (written) for the currently executing instruction. Make the necessary changes to the control unit.
  //   You should modify the control unit test cases to also test FLEN.
  //   Although the pc register is logically part of the register file, it is read and written on every cycle independent of the normal register file operation. 
  //   A question arises if we should build pc as a standalone register or as part of the register file. Consider the pros and cons of both approaches in your implementation. 
  //   Option 1: pc inside the register file How do we interface the pc register with memory for fetching instructions? 
  //   Option 2: pc outside the register file How do instructions read from and write to the pc? 
  //   Option 3: pc is somewhere else We leave this to your creativity!
  //   I Put the PC in its own component. I did this because i feel like the PC's purpose is fundementally different to all the other registers. 
  //   The PC is always either incrementing or loading a new value, (always written to). Where as other registers (including the flag register) only sometimes load.
  //   Hence the PC is its own register
endmodule
