// Digital circuit reg_file-extended.dig as structural Verilog
module reg_file_extended (
  input  [2:0] RS1,
  input  [2:0] RS2,
  input  [2:0] WS,
  input  WE,
  input  [15:0] IN,
  input  clk,
  input  FL_EN,
  input  [3:0] FL_IN,
  input  SETH,
  output [15:0] OUT1,
  output [15:0] OUT2,
  output Z_REG,
  output [15:0] ADDRESS
);

  wire demultiplexer_1_out_1, demultiplexer_1_out_2, demultiplexer_1_out_3, demultiplexer_1_out_4,
       demultiplexer_1_out_6, demultiplexer_1_out_7;
  wire [15:0] pc_extended_1_p1, pc_extended_1_p6, R1_q, R2_q, R3_q, R4_q, R6_q, seth_extended_1_p28;
  wire [15:1] FL_q;

  Demultiplexer #(.Selector_Bits(3)) demultiplexer_1 (
    .sel(WS), .in(WE), .out_1(demultiplexer_1_out_1), .out_2(demultiplexer_1_out_2),
    .out_3(demultiplexer_1_out_3), .out_4(demultiplexer_1_out_4), .out_6(demultiplexer_1_out_6),
    .out_7(demultiplexer_1_out_7));  // open: out_0, out_5
  Register #(.Bits(16)) R1 (.D(pc_extended_1_p1), .C(clk), .en(demultiplexer_1_out_1), .Q(R1_q));
  Register #(.Bits(16)) R2 (.D(pc_extended_1_p1), .C(clk), .en(demultiplexer_1_out_2), .Q(R2_q));
  Register #(.Bits(16)) R3 (.D(pc_extended_1_p1), .C(clk), .en(demultiplexer_1_out_3), .Q(R3_q));
  Register #(.Bits(16)) R4 (.D(pc_extended_1_p1), .C(clk), .en(demultiplexer_1_out_4), .Q(R4_q));
  Register #(.Bits(16)) FL (.D({{12{1'b0}}, FL_IN}), .C(clk), .en(FL_EN), .Q({FL_q, Z_REG}));
  // PC_extended pc_extended_1: pin names not known; wires that end beside it: pc_extended_1_p1, demultiplexer_1_out_7, clk, WS, ADDRESS, pc_extended_1_p6
  Register #(.Bits(16)) R6 (.D(pc_extended_1_p1), .C(clk), .en(demultiplexer_1_out_6), .Q(R6_q));
  // seth_extended seth_extended_1: pin names not known; wires that end beside it: demultiplexer_1_out_1, demultiplexer_1_out_2, demultiplexer_1_out_3, demultiplexer_1_out_4, demultiplexer_1_out_6, demultiplexer_1_out_7, pc_extended_1_p1, {{12{1'b0}}, FL_IN}, FL_EN, clk, pc_extended_1_p1, ADDRESS, {FL_q, Z_REG}, R4_q, R3_q, R2_q, R1_q, IN, SETH, ADDRESS, R1_q, R2_q, R3_q, R4_q, {FL_q, Z_REG}, R6_q, {16{1'b0}}, seth_extended_1_p28
  Multiplexer #(.Selector_Bits(3), .Bits(16)) multiplexer_1 (
    .sel(RS1), .in_0({16{1'b0}}), .in_1(R1_q), .in_2(R2_q), .in_3(R3_q), .in_4(R4_q), .in_5({FL_q, Z_REG}),
    .in_6(R6_q), .in_7(ADDRESS), .out(OUT1));
  Multiplexer #(.Selector_Bits(3), .Bits(16)) multiplexer_2 (
    .sel(RS2), .in_0({16{1'b0}}), .in_1(R1_q), .in_2(R2_q), .in_3(R3_q), .in_4(R4_q), .in_5({FL_q, Z_REG}),
    .in_6(R6_q), .in_7(ADDRESS), .out(OUT2));
  // NotConnected on pc_extended_1_p6
  // NotConnected on seth_extended_1_p28

  // Other names for the same wires on the sheet: IN_OLD[15:0] = IN

  // Notes on the sheet:
  //   RS1: The index of the register which should output its value to OUT1.
  //   RS2: The index of the register which should output its value to OUT2.
  //   WS: The index of the register which should save the value on IN on the next clock cycle (if WE is high).
  //   WE: Whether the register selected by WS should save the value from IN on the next cycle.
  //   IN: The value to be saved into the register specified by WS if WE is high,
  //   OUT1: The value in the register specified by RS1.
  //   OUT2: The value in the register specified by RS2.
  //   FL_EN: Determines whether the Flag register 
  //   should be written to or not
  //   FL_IN: The flag value outputted by the ALU
  //   Z_REG: The z flag stored in the flag register
  //   SETH: if the seth instruction was called
endmodule

/* Test case General:
clk RS1 RS2 WS WE IN OUT1 OUT2
c 0 0 0 1 0x1234 0x0000 0x0000
c 1 0 1 1 0xBEEF 0xBEEF 0x0000
c 2 1 2 1 0xDEAD 0xDEAD 0xBEEF
c 3 2 3 1 0xFFFF 0xFFFF 0xDEAD
c 3 2 3 0 0xABCD 0xFFFF 0xDEAD
c 3 2 2 0 0xABCD 0xFFFF 0xDEAD
c 1 0 1 0 0xABCD 0xBEEF 0x0000
c 1 0 0 0 0xABCD 0xBEEF 0x0000
c 1 0 2 1 0xBADE 0xBEEF 0x0000
c 0 2 2 1 0xBADE 0x0000 0xBADE
c 0 0 2 0 0x1234 0x0000 0x0000
c 2 3 0 1 0x0000 0xBADE 0xFFFF
c 0 0 2 0 0x1234 0x0000 0x0000
*/

/* Test case Flag:
clk FL_IN FL_EN Z_REG
0     0    0       0
c     3    1       3
c     2    0       3
c     2    1       2
c     0    0       2
c     0    1       0
*/

/* Test case Load PC:
clk IN WS WE ADDRESS
0   0  000 1    0
loop(a,10)
c   0  000 1   (a+1)
end loop
c   0  111 1     0 # overwrite PC here
loop(a,10)
c   0  000 1   (a+1)
end loop
*/
