// Digital circuit seth-basic.dig as structural Verilog
module seth_basic (
  input  SETH,
  input  [15:0] INOLD,
  input  [15:0] R1,
  input  [15:0] R2,
  input  [15:0] R3,
  input  [15:0] R4,
  input  [15:0] FL,
  input  [15:0] PC,
  input  [2:0] WS,
  output [15:0] IN
);

  wire [15:0] multiplexer_1_out, notconnected_1_out;

  Multiplexer #(.Selector_Bits(3), .Bits(16)) multiplexer_1 (
    .sel(WS), .in_0({16{1'b0}}), .in_1(R1), .in_2(R2), .in_3(R3), .in_4(R4), .in_5(FL),
    .in_6(notconnected_1_out), .in_7(PC), .out(multiplexer_1_out));
  // NotConnected on notconnected_1_out
  Multiplexer #(.Bits(16)) multiplexer_2 (
    .sel(SETH), .in_0(INOLD), .in_1({INOLD[7:0], multiplexer_1_out[7:0]}), .out(IN));

  // Notes on the sheet:
  //   SETH: if the seth instruction was called
  //   INOLD: The value to be saved into the register specified by WS if WE is high,
  //   R1: The value to be saved into the register specified by WS if WE is high,
  //   R2: The value to be saved into the register specified by WS if WE is high,
  //   R3: The value to be saved into the register specified by WS if WE is high,
  //   R4: The value to be saved into the register specified by WS if WE is high,
  //   FL: The value to be saved into the register specified by WS if WE is high,
  //   PC: The value to be saved into the register specified by WS if WE is high,
  //   WS: The index of the register which should save the value on IN on the next clock cycle (if WE is high).
endmodule

/* Test case SETH:
R1    R2    R3    R4     FL    PC    WS    INOLD   SETH    IN
0x12  0     0    0x24    0x11  0x1   1     0x34     0    0x34
0x12  0     0    0x24    0x11  0x1   1     0x34     1    0x3412 
0x12  0     0    0x24    0x11  0x1   2     0x34     1    0x3400
0x12  0     0    0x24    0x11  0x1   3     0x34     1    0x3400
0x12  0     0    0x24    0x11  0x1   4     0x34     1    0x3424
0x12  0     0    0x24    0x11  0x1   5     0x34     1    0x3411
0x12  0     0    0x24    0x11  0x1   7     0x34     1    0x3401
*/
